# Fritzing sketch WS2812B Lantern (saved by Fritzing 0.9.2b)
circuit board: 8.46667cm x 5.64444cm
breadboards: 1

parts:
  U1 = attiny85 [package=dip]
  IC1 = Voltage Regulator [package=to220-igo]
  VCC1 = Battery block 9V
  S1 = Toggle Switch [package=THT]
  neopixel1 = Neopixel 24 Ring
  S2 = Momentary Switch [package=ksa_sealed_tac_switch]

nets:
  N1: U1.Pin_1, U1.Pin_8, IC1.OUT, neopixel1.Vcc
  N2: U1.Pin_3, neopixel1.IN
  N3: U1.Pin_4, IC1.IN, VCC1.-, neopixel1.GND, S2.1, S2.2
  N4: U1.Pin_5, S2.3, S2.4
  N5: IC1.GND, S1.L2
  N6: VCC1.+, S1.L1
